// Logisim project ALU.circ as structural Verilog
module OF (
  input  a,
  input  BInvert,
  input  b,
  input  Res,
  output Set,
  output OF
);

  wire and_1_out, and_2_out, and_3_out, not_1_out, not_2_out, not_3_out;

  and and_1 (and_1_out, a, BInvert, b);
  not not_1 (not_1_out, a);
  and and_2 (and_2_out, not_1_out, not_2_out, Res);
  not not_2 (not_2_out, b);
  and and_3 (and_3_out, a, b, not_3_out);
  not not_3 (not_3_out, Res);
  or or_1 (Set, Res, and_1_out);
  or or_2 (OF, and_2_out, and_3_out);
endmodule

module _1BitALU (
  input  Ainvert,
  input  CarryIn,
  input  [1:0] Operation,
  input  Binvert,
  input  a,
  input  b,
  input  less,
  output g,
  output p,
  output Result,
  output Set,
  output OF,
  output CarryOut
);

  wire adder_1_out, multiplexer_1_out, multiplexer_2_out, not_1_out, not_2_out;

  Multiplexer multiplexer_1 (.in0(a), .in1(not_1_out), .out(multiplexer_1_out), .sel(Ainvert), .en(1'b1));
  not not_1 (not_1_out, a);
  not not_2 (not_2_out, b);
  Multiplexer multiplexer_2 (.in0(b), .in1(not_2_out), .out(multiplexer_2_out), .sel(Binvert), .en(1'b1));
  OF of_1 (.a(multiplexer_1_out), .BInvert(Binvert), .b(multiplexer_2_out), .Res(adder_1_out), .Set(Set), .OF(OF));
  and and_1 (g, multiplexer_1_out, multiplexer_2_out);
  or or_1 (p, multiplexer_1_out, multiplexer_2_out);
  Adder #(.width(1)) adder_1 (
    .a(multiplexer_1_out), .b(multiplexer_2_out), .out(adder_1_out), .cin(CarryIn), .cout(CarryOut));
  Multiplexer #(.select(2)) multiplexer_3 (
    .in0(g), .in1(p), .in2(adder_1_out), .in3(less), .out(Result), .sel(Operation), .en(1'b1));

  // Notes on the sheet:
  //   less: pull=down
endmodule

module _74182 (
  input  G4,
  input  P4,
  input  G3,
  input  P3,
  input  G2,
  input  P2,
  input  G1,
  input  P1,
  input  Cin,
  output C4,
  output C3,
  output C2,
  output C1,
  output G_star,
  output P_star
);

  wire and_2_out, and_3_out, and_4_out, and_5_out, and_6_out, and_7_out, and_8_out, and_9_out, and_10_out,
       and_11_out;

  and and_1 (P_star, P4, P3, P2, P1);
  or or_1 (G_star, and_4_out, and_2_out, and_3_out, G4);
  and and_2 (and_2_out, P4, P3, G2);
  and and_3 (and_3_out, P4, G3);
  or or_2 (C4, G4, and_3_out, and_2_out, and_4_out, and_5_out);
  and and_4 (and_4_out, P4, P3, P2, G1);
  and and_5 (and_5_out, P4, P3, P2, P1, Cin);
  and and_6 (and_6_out, P3, G2);
  or or_3 (C3, G3, and_6_out, and_7_out, and_8_out);
  and and_7 (and_7_out, P3, P2, G1);
  or or_4 (C2, G2, and_9_out, and_10_out);
  and and_8 (and_8_out, P3, P2, P1, Cin);
  and and_9 (and_9_out, P2, G1);
  and and_10 (and_10_out, P2, P1, Cin);
  or or_5 (C1, G1, and_11_out);
  and and_11 (and_11_out, P1, Cin);

  // Notes on the sheet:
  //   P2: pull=down
  //   G2: pull=down
  //   G4: pull=down
  //   P4: pull=down
  //   P3: pull=down
  //   G3: pull=down
  //   P1: pull=down
  //   Cin: pull=down
  //   G1: pull=down
  //   输入引脚区
  //   4位先行进位电路
  //   请根据以上引脚以及隧道信号设计完成74LS182先行进位电路，尽可能使用多输入逻辑门，并分析电路延迟
  //   输出引脚区
endmodule

module _4BitALU (
  input  [3:0] X,
  input  [3:0] Y,
  input  [1:0] Op,
  input  Cin,
  input  AInvert,
  input  BInvert,
  input  Less,
  output Z,
  output [3:0] S,
  output C,
  output OF,
  output G_star,
  output P_star,
  output Set
);

  wire n1bitalu_1_g, n1bitalu_1_p, n1bitalu_2_g, n1bitalu_2_p, n1bitalu_3_g, n1bitalu_3_p, n1bitalu_4_g,
       n1bitalu_4_p, n74182_1_c1, n74182_1_c2, n74182_1_c3, or_1_out;

  not not_1 (Z, or_1_out);
  or or_1 (or_1_out, S[3], S[2], S[1], S[0]);
  _1BitALU u_1bitalu_1 (
    .a(X[0]), .b(Y[0]), .less(Less), .g(n1bitalu_1_g), .p(n1bitalu_1_p), .Result(S[0]), .Ainvert(AInvert),
    .Binvert(BInvert), .CarryIn(Cin), .Operation(Op));  // open: Set, OF, CarryOut
  _1BitALU u_1bitalu_2 (
    .a(X[1]), .b(Y[1]), .g(n1bitalu_2_g), .p(n1bitalu_2_p), .Result(S[1]), .Ainvert(AInvert),
    .Binvert(BInvert), .CarryIn(n74182_1_c1), .Operation(Op));  // open: less, Set, OF, CarryOut
  _1BitALU u_1bitalu_3 (
    .a(X[2]), .b(Y[2]), .g(n1bitalu_3_g), .p(n1bitalu_3_p), .Result(S[2]), .Ainvert(AInvert),
    .Binvert(BInvert), .CarryIn(n74182_1_c2), .Operation(Op));  // open: less, Set, OF, CarryOut
  _1BitALU u_1bitalu_4 (
    .a(X[3]), .b(Y[3]), .g(n1bitalu_4_g), .p(n1bitalu_4_p), .Result(S[3]), .Set(Set), .OF(OF),
    .Ainvert(AInvert), .Binvert(BInvert), .CarryIn(n74182_1_c3), .Operation(Op));  // open: less, CarryOut
  // Probe on X
  // Probe on Y
  // Probe on S
  _74182 u_74182_1 (
    .G4(n1bitalu_4_g), .P4(n1bitalu_4_p), .G3(n1bitalu_3_g), .P3(n1bitalu_3_p), .G2(n1bitalu_2_g),
    .P2(n1bitalu_2_p), .G1(n1bitalu_1_g), .P1(n1bitalu_1_p), .Cin(Cin), .C4(C), .C3(n74182_1_c3),
    .C2(n74182_1_c2), .C1(n74182_1_c1), .G_star(G_star), .P_star(P_star));
  // Probe on X
  // Probe on Y
  // Probe on S

  // Notes on the sheet:
  //   Y: pull=down
  //   X: pull=down
  //   Less: pull=down
  //   输入引脚区
  //   输出引脚区
  //   +
  //   =
  //   有符号加法
  //   +
  //   =
  //   无符号加法
endmodule

module _32BitALU (
  input  [3:0] ALUOp,
  input  [31:0] X,
  input  [31:0] Y,
  output C32,
  output C31,
  output [31:0] S
);

  wire n4bitalu_1_g_star, n4bitalu_1_p_star, n4bitalu_2_g_star, n4bitalu_2_p_star, n4bitalu_3_g_star,
       n4bitalu_3_p_star, n4bitalu_4_g_star, n4bitalu_4_p_star, n4bitalu_5_g_star, n4bitalu_5_p_star,
       n4bitalu_6_g_star, n4bitalu_6_p_star, n4bitalu_7_g_star, n4bitalu_7_p_star, n4bitalu_8_g_star,
       n4bitalu_8_p_star, n74182_1_c1, n74182_1_c2, n74182_1_c3, n74182_1_c4, n74182_2_c1, n74182_2_c2,
       n74182_2_c3;

  _4BitALU u_4bitalu_1 (
    .X(X[3:0]), .Y(Y[3:0]), .AInvert(ALUOp[3]), .BInvert(ALUOp[2]), .S(S[3:0]), .G_star(n4bitalu_1_g_star),
    .Op(ALUOp[1:0]), .P_star(n4bitalu_1_p_star), .Cin(ALUOp[2]));  // open: Less, Z, C, OF, Set
  _4BitALU u_4bitalu_2 (
    .X(X[7:4]), .Y(Y[7:4]), .AInvert(ALUOp[3]), .BInvert(ALUOp[2]), .S(S[7:4]), .G_star(n4bitalu_2_g_star),
    .Op(ALUOp[1:0]), .P_star(n4bitalu_2_p_star), .Cin(n74182_1_c1));  // open: Less, Z, C, OF, Set
  _4BitALU u_4bitalu_3 (
    .X(X[11:8]), .Y(Y[11:8]), .AInvert(ALUOp[3]), .BInvert(ALUOp[2]), .S(S[11:8]),
    .G_star(n4bitalu_3_g_star), .Op(ALUOp[1:0]), .P_star(n4bitalu_3_p_star), .Cin(n74182_1_c2));  // open: Less, Z, C, OF, Set
  _4BitALU u_4bitalu_4 (
    .X(X[15:12]), .Y(Y[15:12]), .AInvert(ALUOp[3]), .BInvert(ALUOp[2]), .S(S[15:12]),
    .G_star(n4bitalu_4_g_star), .Op(ALUOp[1:0]), .P_star(n4bitalu_4_p_star), .Cin(n74182_1_c3));  // open: Less, Z, C, OF, Set
  _74182 u_74182_1 (
    .G4(n4bitalu_4_g_star), .P4(n4bitalu_4_p_star), .G3(n4bitalu_3_g_star), .P3(n4bitalu_3_p_star),
    .G2(n4bitalu_2_g_star), .P2(n4bitalu_2_p_star), .G1(n4bitalu_1_g_star), .P1(n4bitalu_1_p_star),
    .Cin(ALUOp[2]), .C4(n74182_1_c4), .C3(n74182_1_c3), .C2(n74182_1_c2), .C1(n74182_1_c1));  // open: G_star, P_star
  _4BitALU u_4bitalu_5 (
    .X(X[19:16]), .Y(Y[19:16]), .AInvert(ALUOp[3]), .BInvert(ALUOp[2]), .S(S[19:16]),
    .G_star(n4bitalu_5_g_star), .Op(ALUOp[1:0]), .P_star(n4bitalu_5_p_star), .Cin(n74182_1_c4));  // open: Less, Z, C, OF, Set
  _4BitALU u_4bitalu_6 (
    .X(X[23:20]), .Y(Y[23:20]), .AInvert(ALUOp[3]), .BInvert(ALUOp[2]), .S(S[23:20]),
    .G_star(n4bitalu_6_g_star), .Op(ALUOp[1:0]), .P_star(n4bitalu_6_p_star), .Cin(n74182_2_c1));  // open: Less, Z, C, OF, Set
  _4BitALU u_4bitalu_7 (
    .X(X[27:24]), .Y(Y[27:24]), .AInvert(ALUOp[3]), .BInvert(ALUOp[2]), .S(S[27:24]),
    .G_star(n4bitalu_7_g_star), .Op(ALUOp[1:0]), .P_star(n4bitalu_7_p_star), .Cin(n74182_2_c2));  // open: Less, Z, C, OF, Set
  _4BitALU u_4bitalu_8 (
    .X(X[31:28]), .Y(Y[31:28]), .AInvert(ALUOp[3]), .BInvert(ALUOp[2]), .S(S[31:28]),
    .G_star(n4bitalu_8_g_star), .Op(ALUOp[1:0]), .P_star(n4bitalu_8_p_star), .Cin(n74182_2_c3));  // open: Less, Z, C, OF, Set
  _74182 u_74182_2 (
    .G4(n4bitalu_8_g_star), .P4(n4bitalu_8_p_star), .G3(n4bitalu_7_g_star), .P3(n4bitalu_7_p_star),
    .G2(n4bitalu_6_g_star), .P2(n4bitalu_6_p_star), .G1(n4bitalu_5_g_star), .P1(n4bitalu_5_p_star),
    .Cin(n74182_1_c4), .C3(n74182_2_c3), .C2(n74182_2_c2), .C1(n74182_2_c1));  // open: C4, G_star, P_star
  // Probe on X
  // Probe on Y
  // Probe on S
  // Probe on X
  // Probe on Y
  // Probe on S

  // Other names for the same wires on the sheet: Op[1:0] = ALUOp[1:0]; BInvert = ALUOp[2]; AInvert = ALUOp[3];
  //   S0[3:0] = S[3:0]; S1[3:0] = S[7:4]; S2[3:0] = S[11:8]; S3[3:0] = S[15:12]; S4[3:0] = S[19:16];
  //   S5[3:0] = S[23:20]; S6[3:0] = S[27:24]; S7[3:0] = S[31:28]; X0[3:0] = X[3:0]; X1[3:0] = X[7:4];
  //   X2[3:0] = X[11:8]; X3[3:0] = X[15:12]; X4[3:0] = X[19:16]; X5[3:0] = X[23:20]; X6[3:0] = X[27:24];
  //   X7[3:0] = X[31:28]; Y0[3:0] = Y[3:0]; Y1[3:0] = Y[7:4]; Y2[3:0] = Y[11:8]; Y3[3:0] = Y[15:12];
  //   Y4[3:0] = Y[19:16]; Y5[3:0] = Y[23:20]; Y6[3:0] = Y[27:24]; Y7[3:0] = Y[31:28]

  // Notes on the sheet:
  //   Y: pull=down
  //   X: pull=down
  //   输入引脚区
  //   输出引脚区
  //   +
  //   =
  //   有符号加法
  //   +
  //   =
  //   无符号加法
endmodule
