// Logisim project MIPSCpu.circ as structural Verilog
module ALUControl (
  input  ALUOp1,
  input  ALUOp0,
  input  F5,
  input  F4,
  input  F3,
  input  F2,
  input  F1,
  input  F0,
  output Op3,
  output Op2,
  output Op1,
  output Op0
);

  wire and_1_out, and_2_out, and_4_out, and_5_out, and_6_out, and_7_out, not_1_out, not_2_out, not_3_out,
       not_4_out, not_5_out, not_6_out, not_7_out, not_8_out, not_9_out, not_10_out, not_11_out, not_12_out,
       not_13_out, not_14_out, not_15_out, not_16_out;

  not not_1 (not_1_out, F3);
  not not_2 (not_2_out, F0);
  not not_3 (not_3_out, F3);
  not not_4 (not_4_out, F0);
  not not_5 (not_5_out, F2);
  not not_6 (not_6_out, F0);
  not not_7 (not_7_out, ALUOp1);
  not not_8 (not_8_out, F3);
  not not_9 (not_9_out, F2);
  and and_1 (and_1_out, not_8_out, not_9_out, not_10_out);
  not not_10 (not_10_out, F0);
  not not_11 (not_11_out, F2);
  and and_2 (and_2_out, not_11_out, F1, not_12_out);
  not not_12 (not_12_out, F0);
  not not_13 (not_13_out, F3);
  not not_14 (not_14_out, F1);
  not not_15 (not_15_out, F2);
  not not_16 (not_16_out, F0);
  and and_3 (Op3, ALUOp1, not_1_out, F2, F1, not_2_out);
  or or_1 (Op2, ALUOp0, and_4_out, and_5_out);
  and and_4 (and_4_out, ALUOp1, not_3_out, F1, not_4_out);
  and and_5 (and_5_out, ALUOp1, not_5_out, F1, not_6_out);
  or or_2 (Op1, not_7_out, and_1_out, and_2_out, ALUOp0);
  and and_6 (and_6_out, ALUOp1, not_13_out, F2, not_14_out, F0);
  or or_3 (Op0, and_6_out, and_7_out);
  and and_7 (and_7_out, ALUOp1, F3, not_15_out, F1, not_16_out);
endmodule

module Control (
  input  Op5,
  input  Op4,
  input  Op3,
  input  Op2,
  input  Op1,
  input  Op0,
  output RegDst,
  output ALUSrc,
  output MemtoReg,
  output RegWrite,
  output MemRead,
  output MemWrite,
  output Branch,
  output ALUOp1,
  output ALUOp0
);

  wire and_4_out, and_5_out, not_1_out, not_2_out, not_3_out, not_4_out, not_5_out, not_6_out, not_7_out,
       not_8_out, not_9_out, not_10_out, not_11_out, not_12_out, not_13_out, not_14_out, not_15_out,
       not_16_out, not_17_out, not_18_out, not_19_out, not_20_out, not_21_out, not_22_out, not_23_out,
       not_24_out, not_25_out, not_26_out, not_27_out, not_28_out, not_29_out, not_30_out, not_31_out,
       not_32_out, not_33_out, not_34_out, not_35_out, not_36_out, not_37_out, not_38_out, not_39_out,
       not_40_out, not_41_out;

  not not_1 (not_1_out, Op5);
  not not_2 (not_2_out, Op4);
  not not_3 (not_3_out, Op3);
  not not_4 (not_4_out, Op2);
  not not_5 (not_5_out, Op1);
  not not_6 (not_6_out, Op0);
  not not_7 (not_7_out, Op4);
  not not_8 (not_8_out, Op2);
  not not_9 (not_9_out, Op4);
  not not_10 (not_10_out, Op3);
  not not_11 (not_11_out, Op2);
  not not_12 (not_12_out, Op5);
  not not_13 (not_13_out, Op4);
  not not_14 (not_14_out, Op3);
  not not_15 (not_15_out, Op2);
  not not_16 (not_16_out, Op1);
  not not_17 (not_17_out, Op0);
  not not_18 (not_18_out, Op4);
  not not_19 (not_19_out, Op3);
  not not_20 (not_20_out, Op2);
  not not_21 (not_21_out, Op4);
  not not_22 (not_22_out, Op3);
  not not_23 (not_23_out, Op2);
  not not_24 (not_24_out, Op4);
  not not_25 (not_25_out, Op2);
  not not_26 (not_26_out, Op5);
  not not_27 (not_27_out, Op4);
  not not_28 (not_28_out, Op3);
  not not_29 (not_29_out, Op1);
  not not_30 (not_30_out, Op0);
  not not_31 (not_31_out, Op5);
  not not_32 (not_32_out, Op4);
  not not_33 (not_33_out, Op3);
  not not_34 (not_34_out, Op2);
  not not_35 (not_35_out, Op1);
  not not_36 (not_36_out, Op0);
  not not_37 (not_37_out, Op5);
  not not_38 (not_38_out, Op4);
  not not_39 (not_39_out, Op3);
  not not_40 (not_40_out, Op1);
  not not_41 (not_41_out, Op0);
  and and_1 (RegDst, not_1_out, not_2_out, not_3_out, not_4_out, not_5_out, not_6_out);
  and and_2 (ALUSrc, Op5, not_7_out, not_8_out, Op1, Op0);
  and and_3 (MemtoReg, Op5, not_9_out, not_10_out, not_11_out, Op1, Op0);
  and and_4 (and_4_out, not_12_out, not_13_out, not_14_out, not_15_out, not_16_out, not_17_out);
  and and_5 (and_5_out, Op5, not_18_out, not_19_out, not_20_out, Op1, Op0);
  and and_6 (MemRead, Op5, not_21_out, not_22_out, not_23_out, Op1, Op0);
  and and_7 (MemWrite, Op5, not_24_out, Op3, not_25_out, Op1, Op0);
  and and_8 (Branch, not_26_out, not_27_out, not_28_out, Op2, not_29_out, not_30_out);
  and and_9 (ALUOp1, not_31_out, not_32_out, not_33_out, not_34_out, not_35_out, not_36_out);
  and and_10 (ALUOp0, not_37_out, not_38_out, not_39_out, Op2, not_40_out, not_41_out);
  or or_1 (RegWrite, and_4_out, and_5_out);
endmodule

module ALU (
  input  [3:0] Op,
  input  Enable,
  input  [31:0] A,
  input  [31:0] B,
  output [31:0] Ressult,
  output Zero
);

  wire n8_bitalu_1_carryout, n8_bitalu_1_resor, n8_bitalu_2_carryout, n8_bitalu_2_resor,
       n8_bitalu_3_carryout, n8_bitalu_3_resor, n8_bitalu_4_resor, n8_bitalu_4_set;

  _8_BitALU u_8_bitalu_1 (
    .Less(n8_bitalu_4_set), .A(A[7:0]), .B(B[7:0]), .AInvert(Op[3]), .BInvert(Op[2]), .CarryIn(Op[2]),
    .Enable(Enable), .Op(Op[1:0]), .CarryOut(n8_bitalu_1_carryout), .Result(Ressult[7:0]),
    .ResOr(n8_bitalu_1_resor));  // open: Set
  _8_BitALU u_8_bitalu_2 (
    .A(A[15:8]), .B(B[15:8]), .AInvert(Op[3]), .BInvert(Op[2]), .CarryIn(n8_bitalu_1_carryout),
    .Enable(Enable), .Op(Op[1:0]), .CarryOut(n8_bitalu_2_carryout), .Result(Ressult[15:8]),
    .ResOr(n8_bitalu_2_resor));  // open: Less, Set
  _8_BitALU u_8_bitalu_3 (
    .A(A[23:16]), .B(B[23:16]), .AInvert(Op[3]), .BInvert(Op[2]), .CarryIn(n8_bitalu_2_carryout),
    .Enable(Enable), .Op(Op[1:0]), .CarryOut(n8_bitalu_3_carryout), .Result(Ressult[23:16]),
    .ResOr(n8_bitalu_3_resor));  // open: Less, Set
  _8_BitALU u_8_bitalu_4 (
    .A(A[31:24]), .B(B[31:24]), .AInvert(Op[3]), .BInvert(Op[2]), .CarryIn(n8_bitalu_3_carryout),
    .Enable(Enable), .Op(Op[1:0]), .Result(Ressult[31:24]), .ResOr(n8_bitalu_4_resor), .Set(n8_bitalu_4_set));  // open: Less, CarryOut
  nor nor_1 (Zero, n8_bitalu_1_resor, n8_bitalu_2_resor, n8_bitalu_3_resor, n8_bitalu_4_resor);
endmodule

module _8_BitALU (
  input  AInvert,
  input  BInvert,
  input  CarryIn,
  input  Enable,
  input  [1:0] Op,
  input  Less,
  input  [7:0] A,
  input  [7:0] B,
  output [7:0] Result,
  output ResOr,
  output Set,
  output CarryOut
);

  wire n1_bitalu_1_carryout, n1_bitalu_2_carryout, n1_bitalu_3_carryout, n1_bitalu_4_carryout,
       n1_bitalu_5_carryout, n1_bitalu_6_carryout, n1_bitalu_7_carryout;

  _1_BitALU u_1_bitalu_1 (
    .a(A[0]), .b(B[0]), .less(Less), .Ainvert(AInvert), .Binvert(BInvert), .CarryIn(CarryIn),
    .Enable(Enable), .Operation(Op), .CarryOut(n1_bitalu_1_carryout), .Result(Result[0]));  // open: Set
  _1_BitALU u_1_bitalu_2 (
    .a(A[1]), .b(B[1]), .Ainvert(AInvert), .Binvert(BInvert), .CarryIn(n1_bitalu_1_carryout),
    .Enable(Enable), .Operation(Op), .CarryOut(n1_bitalu_2_carryout), .Result(Result[1]));  // open: less, Set
  _1_BitALU u_1_bitalu_3 (
    .a(A[2]), .b(B[2]), .Ainvert(AInvert), .Binvert(BInvert), .CarryIn(n1_bitalu_2_carryout),
    .Enable(Enable), .Operation(Op), .CarryOut(n1_bitalu_3_carryout), .Result(Result[2]));  // open: less, Set
  _1_BitALU u_1_bitalu_4 (
    .a(A[3]), .b(B[3]), .Ainvert(AInvert), .Binvert(BInvert), .CarryIn(n1_bitalu_3_carryout),
    .Enable(Enable), .Operation(Op), .CarryOut(n1_bitalu_4_carryout), .Result(Result[3]));  // open: less, Set
  _1_BitALU u_1_bitalu_5 (
    .a(A[4]), .b(B[4]), .Ainvert(AInvert), .Binvert(BInvert), .CarryIn(n1_bitalu_4_carryout),
    .Enable(Enable), .Operation(Op), .CarryOut(n1_bitalu_5_carryout), .Result(Result[4]));  // open: less, Set
  _1_BitALU u_1_bitalu_6 (
    .a(A[5]), .b(B[5]), .Ainvert(AInvert), .Binvert(BInvert), .CarryIn(n1_bitalu_5_carryout),
    .Enable(Enable), .Operation(Op), .CarryOut(n1_bitalu_6_carryout), .Result(Result[5]));  // open: less, Set
  _1_BitALU u_1_bitalu_7 (
    .a(A[6]), .b(B[6]), .Ainvert(AInvert), .Binvert(BInvert), .CarryIn(n1_bitalu_6_carryout),
    .Enable(Enable), .Operation(Op), .CarryOut(n1_bitalu_7_carryout), .Result(Result[6]));  // open: less, Set
  _1_BitALU u_1_bitalu_8 (
    .a(A[7]), .b(B[7]), .Ainvert(AInvert), .Binvert(BInvert), .CarryIn(n1_bitalu_7_carryout),
    .Enable(Enable), .Operation(Op), .CarryOut(CarryOut), .Result(Result[7]), .Set(Set));  // open: less
  or or_1 (ResOr, Result[0], Result[1], Result[2], Result[3], Result[4], Result[5], Result[6], Result[6]);

  // Other names for the same wires on the sheet: Res0 = Result[0]; Res1 = Result[1]; Res2 = Result[2];
  //   Res3 = Result[3]; Res4 = Result[4]; Res5 = Result[5]; Res6 = Result[6]; Res7 = Result[7]

  // Notes on the sheet:
  //   Less: pull=down
  //   Enable: pull=up
endmodule

module _1_BitALU (
  input  Ainvert,
  input  CarryIn,
  input  [1:0] Operation,
  input  Binvert,
  input  Enable,
  input  a,
  input  b,
  input  less,
  output Result,
  output Set,
  output CarryOut
);

  wire and_1_out, multiplexer_1_out, multiplexer_2_out, not_1_out, not_2_out, or_1_out;

  not not_1 (not_1_out, a);
  Multiplexer multiplexer_1 (.in0(a), .in1(not_1_out), .out(multiplexer_1_out), .sel(Ainvert), .en(Enable));
  Multiplexer multiplexer_2 (.in0(b), .in1(not_2_out), .out(multiplexer_2_out), .sel(Binvert), .en(Enable));
  not not_2 (not_2_out, b);
  and and_1 (and_1_out, multiplexer_1_out, multiplexer_2_out);
  or or_1 (or_1_out, multiplexer_1_out, multiplexer_2_out);
  Adder #(.width(1)) adder_1 (.a(multiplexer_1_out), .b(multiplexer_2_out), .out(Set), .cin(CarryIn), .cout(CarryOut));
  Multiplexer #(.select(2)) multiplexer_3 (
    .in0(and_1_out), .in1(or_1_out), .in2(Set), .in3(less), .out(Result), .sel(Operation), .en(Enable));

  // Notes on the sheet:
  //   less: pull=down
  //   Enable: pull=up
endmodule
